# Fritzing sketch wire connections (saved by Fritzing 0.9.4)

parts:
  Part2 = Arduino Mega 2560 (Rev3)
  L298N1 = L298N DC motor driver
  DC_Mot_Enc1 = DC Motor with two-phase hall-encoder [part_number=VT-E-G25A-06-177E]
  VCC2 = Battery
  S1 = Toggle Switch [package=THT]

nets:
  N1: Part2.D10_PWM, L298N1.IN3
  N2: Part2.D9_PWM, L298N1.IN4
  N3: Part2.D8_PWM, L298N1.ENB
  GND: Part2.GND, L298N1.GND, DC_Mot_Enc1.pin5, VCC2.-
  VIN: Part2.VIN, L298N1.12V, S1.L2
  N4: Part2.D2_PWM, DC_Mot_Enc1.pin4
  N5: L298N1.OUT3, DC_Mot_Enc1.pin2
  N6: L298N1.OUT4, DC_Mot_Enc1.pin1
  N7: L298N1.5V, DC_Mot_Enc1.pin6
  N8: VCC2.+, S1.COM

custom parts:
  L298N DC motor driver: 2x DC motor driver with 78M05 positive voltage regulator (7..35 V) L298N: max 46 V, 2 A Set 5 V Enable jumper to enable 5 V regultor (needed for the L298N) and +5 V output at screw terminal or supply external +5 V at screw terminal Set ENA and/or ENB to +5 V to enable motor permanently or supply ENA and/or ENB with PWM signal IN1 and IN2 set rotation directory for motor A (OUT1/OUT2) IN2 and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
  Battery: Your standard 2x 18650 battery pack (7,4 Volts)
